# Fritzing sketch Aufbau (saved by Fritzing 0.9.3b)
breadboards: 1

parts:
  Bauteil1 = Arduino Mega 2560 (Rev3)
  Power_plug1 = Power plug
  Indexfinger = Basic Servo
  Middlefinger = Basic Servo
  Ringfinger = Basic Servo
  Pinky = Basic Servo
  Thump = Basic Servo
  Wrist = Basic Servo

nets:
  GND: Bauteil1.GND, Power_plug1.GND
  N1: Bauteil1.D2_PWM, Thump.pulse
  N2: Bauteil1.D3_PWM, Indexfinger.pulse
  N3: Bauteil1.D4_PWM, Middlefinger.pulse
  N4: Bauteil1.D5_PWM, Ringfinger.pulse
  N5: Bauteil1.D6_PWM, Pinky.pulse
  N6: Bauteil1.D7_PWM, Wrist.pulse

notes:
  Versorgung durch Labornetzteil
